# Fritzing sketch Nodo Xbee (saved by Fritzing 1.0.6)
breadboards: 1

parts:
  Componente1 = Arduino Nano (Rev3.0) (ICSP)
  Componente2 = ACS712 Low Current Sensor Board v12
  Componente3 = XBee Pro RF module
  A1 = AMS11176 module  # not connected

nets:
  N1: Componente1.D2, Componente3.DOUT
  N2: Componente1.D3, Componente3.DIN
  N3: Componente1.D9, Componente3.DTR/SLEEP_RQ/DI8
  N4: Componente1.D10, Componente3.ON/SLEEP
  N5: Componente1.A0, Componente2.VO

custom parts:
  AMS11176 module: DC-DC step-down modules ( input DC 4.5～7V , output DC 3.3V ).
